// Digital circuit RV321_CPU.dig as structural Verilog
module RV321_CPU (
  input  PC_reset,
  input  gt_C_enb,
  input  CLK,
  output [31:0] Q
);

  wire clock_1_gt_c, clock_1_pc_r;
  wire [31:0] pc_1_o_cur, pc_adder_1_n_addr;

  Clock clock_1 (.enb(gt_C_enb), .rst(PC_reset), .CLK_in(CLK), .PC_r(clock_1_pc_r), .gt_C(clock_1_gt_c));
  // Probe on pc_1_o_cur
  PC pc_1 (.rst(clock_1_pc_r), .gt_C(clock_1_gt_c), .def({32{1'b0}}), .addr_in(pc_adder_1_n_addr), .o_cur(pc_1_o_cur));
  // Probe on Q
  ROM #(.AddrBits(24), .isProgramMemory("true"), .Bits(32)) PROG (.A(pc_1_o_cur[23:0]), .sel(1'b1), .D(Q));
  PC_Adder pc_adder_1 (.br_enb(1'b0), .br_off({32{1'b0}}), .o_addr(pc_1_o_cur), .n_addr(pc_adder_1_n_addr));
  Register_File register_file_1 ();  // open: D, gt_C, rs1_addr, rs2_addr, rd_addr, r_enb, w_enb, rs1, rs2
  Immediate_Generator immediate_generator_1 ();  // open: instr, type, imm
  ALU alu_1 ();  // open: op, a, b, shamt, o, zero, SLT, USLT
  RAM ram_1 ();  // open: D, gt_C, w_mask, r_addr, w_addr, r_enb, w_enb, Q

  // Notes on the sheet:
  //   contents of PROG (hex, n*v repeats v):
  //   1,2,6*0,3,17*0,4
endmodule
